// Logisim project Lab4P2Logisim.circ as structural Verilog: 4 circuits, main circuit Simple
module main (
  input  A,
  input  B,
  input  C,
  output X,
  output Y,
  output x_2,
  output y_2
);

  wire and_1_out, and_2_out, and_3_out, nand_1_out, nor_1_out, not_1_out, not_2_out, or_1_out;

  nand nand_1 (nand_1_out, A, B);
  or or_1 (or_1_out, A, C);
  not not_1 (not_1_out, A);
  and and_1 (and_1_out, not_1_out, not_2_out);
  not not_2 (not_2_out, C);
  and and_2 (and_2_out, A, B);
  and and_3 (and_3_out, nand_1_out, or_1_out);
  nor nor_1 (nor_1_out, nand_1_out, or_1_out);
  or or_2 (x_2, and_1_out, and_2_out);
  not not_3 (X, and_3_out);
  not not_4 (Y, nor_1_out);

  assign y_2 = 1'b1;
endmodule

module Simple (
  input  a,
  input  b,
  input  c,
  output x
);

  wire and_1_out, not_1_out, not_2_out, not_3_out;

  not not_1 (not_1_out, a);
  not not_2 (not_2_out, b);
  and and_1 (and_1_out, not_1_out, not_2_out);
  not not_3 (not_3_out, c);
  or or_1 (x, and_1_out, not_3_out);
endmodule

module ninimalized (
  input  a,
  input  b,
  input  c,
  output x
);

  wire and_1_out, and_2_out, not_1_out, not_2_out;

  not not_1 (not_1_out, a);
  not not_2 (not_2_out, c);
  and and_1 (and_1_out, not_1_out, not_2_out);
  and and_2 (and_2_out, a, b);
  or or_1 (x, and_1_out, and_2_out);
endmodule

module minimal3 (
  input  a,
  input  b,
  input  c,
  output x,
  output y
);

  wire and_1_out, and_2_out, not_1_out, not_2_out;

  not not_1 (not_1_out, a);
  not not_2 (not_2_out, c);
  and and_1 (and_1_out, not_1_out, not_2_out);
  and and_2 (and_2_out, a, b);
  or or_1 (x, and_1_out, and_2_out);

  assign y = 1'b1;
endmodule
